// Logisim project pc.circ as structural Verilog: 5 circuits, main circuit main
module main (
  input  in_1
);

  wire clock_1_out;
  wire [11:0] processor_1_out_4;
  wire [15:0] rom_1_data;

  ROM #(.addrWidth(12), .dataWidth(16)) rom_1 (.addr(processor_1_out_4), .data(rom_1_data));  // open: sel
  Clock clock_1 (.out(clock_1_out));
  Processor processor_1 (.clock(clock_1_out), .ins(rom_1_data), .out_4(processor_1_out_4), .reset(in_1));
  DotMatrix #(.matrixcols(32), .matrixrows(32)) dotmatrix_1 ();  // open: col0, col1, col2, col3, col4, col5, col6, col7, col8, col9, col10, col11, col12, col13, col14, col15, col16, col17, col18, col19, col20, col21, col22, col23, col24, col25, col26, col27, col28, col29, col30, col31

  // Notes on the sheet:
  //   contents of rom_1 (hex, n*v repeats v):
  //   80a1 80e0 2001 3001 0 8042 2422 3401
endmodule

module ULA (
  input  [15:0] A,
  input  [3:0] F,
  input  [15:0] B,
  output [15:0] R,
  output FG,
  output FE
);

  wire or_1_out, or_2_out, or_3_out, or_4_out, or_5_out, or_6_out, or_7_out, or_8_out, or_9_out, or_10_out,
       or_11_out, or_12_out, or_13_out, or_14_out, or_15_out, or_16_out, or_17_out, or_18_out, or_19_out,
       or_20_out, or_21_out, or_22_out, or_23_out, or_24_out, or_25_out, or_26_out, or_27_out;
  wire [15:0] and_2_out, and_3_out, and_4_out, and_5_out, and_6_out, and_7_out, and_8_out, and_9_out,
       and_10_out, resltado_divisao, resultado_and, resultado_left_shift, resultado_multicacao,
       resultado_not, resultado_or, resultado_right_shift, resultado_soma, resultado_subtracao;
  wire [15:15] not_1_out, not_2_out, not_3_out, not_4_out, not_5_out, not_6_out, not_7_out, not_8_out,
       not_9_out;

  buf or_1 (or_1_out, F[2]);  // OR_Gate OR_Gate
  buf or_2 (or_2_out, F[2]);  // OR_Gate OR_Gate
  or or_3 (or_3_out, F[2], ~F[3]);  // OR_Gate
  or or_4 (or_4_out, ~F[2], ~F[3]);  // OR_Gate
  buf or_5 (or_5_out, ~F[2]);  // OR_Gate OR_Gate
  buf or_6 (or_6_out, F[2]);  // OR_Gate OR_Gate
  buf or_7 (or_7_out, ~F[2]);  // OR_Gate OR_Gate
  or or_8 (or_8_out, ~F[2], ~F[3]);  // OR_Gate
  or or_9 (or_9_out, F[0], F[1]);
  or or_10 (or_10_out, or_9_out, or_11_out);
  or or_11 (or_11_out, F[2], ~F[3]);  // OR_Gate
  or or_12 (or_12_out, ~F[0], F[1]);  // OR_Gate
  or or_13 (or_13_out, or_12_out, or_1_out);
  or or_14 (or_14_out, F[0], ~F[1]);  // OR_Gate
  or or_15 (or_15_out, or_14_out, or_2_out);
  or or_16 (or_16_out, ~F[0], ~F[1]);  // OR_Gate
  or or_17 (or_17_out, or_16_out, or_3_out);
  or or_18 (or_18_out, F[0], ~F[1]);  // OR_Gate
  or or_19 (or_19_out, or_18_out, or_4_out);
  or or_20 (or_20_out, ~F[0], ~F[1]);  // OR_Gate
  or or_21 (or_21_out, or_20_out, or_5_out);
  or or_22 (or_22_out, F[0], ~F[1]);  // OR_Gate
  or or_23 (or_23_out, or_22_out, or_6_out);
  or or_24 (or_24_out, F[0], F[1]);
  or or_25 (or_25_out, or_24_out, or_7_out);
  or or_26 (or_26_out, ~F[0], F[1]);  // OR_Gate
  or or_27 (or_27_out, or_26_out, or_8_out);
  not not_1 (not_1_out[15], or_10_out);
  not not_2 (not_2_out[15], or_13_out);
  not not_3 (not_3_out[15], or_15_out);
  not not_4 (not_4_out[15], or_17_out);
  not not_5 (not_5_out[15], or_19_out);
  not not_6 (not_6_out[15], or_21_out);
  not not_7 (not_7_out[15], or_23_out);
  not not_8 (not_8_out[15], or_25_out);
  not not_9 (not_9_out[15], or_27_out);
  Adder #(.width(16)) adder_1 (.a(A), .b(B), .out(resultado_soma));  // open: cin, cout
  Subtractor #(.width(16)) subtractor_1 (.a(A), .b(B), .out(resultado_subtracao));  // open: bin, bout
  Multiplier #(.width(16)) multiplier_1 (.a(A), .b(B), .out(resultado_multicacao));  // open: cin, cout
  Divider #(.width(16)) divider_1 (.a(A), .b(B), .out(resltado_divisao));  // open: upper, rem
  assign resultado_and = A & B;  // AND_Gate and_1, 16 bits wide
  assign resultado_or = A | B;  // OR_Gate or_28, 16 bits wide
  assign resultado_not = ~A;  // NOT_Gate not_10, 16 bits wide
  Shifter #(.width(16)) shifter_1 (.in(A), .\dist (B[3:0]), .out(resultado_left_shift));
  Shifter #(.width(16), .shift("lr")) shifter_2 (.in(A), .\dist (B[3:0]), .out(resultado_right_shift));
  Comparator #(.width(16), .mode("unsigned")) comparator_1 (.a(A), .b(B), .gt(FG), .eq(FE));  // open: lt
  assign and_2_out = {16{not_1_out[15]}} & resultado_soma;  // AND_Gate and_2, 16 bits wide
  assign and_3_out = {16{not_2_out[15]}} & resultado_subtracao;  // AND_Gate and_3, 16 bits wide
  assign and_4_out = {16{not_3_out[15]}} & resultado_multicacao;  // AND_Gate and_4, 16 bits wide
  assign and_5_out = {16{not_4_out[15]}} & resltado_divisao;  // AND_Gate and_5, 16 bits wide
  assign and_6_out = {16{not_5_out[15]}} & resultado_and;  // AND_Gate and_6, 16 bits wide
  assign and_7_out = {16{not_6_out[15]}} & resultado_or;  // AND_Gate and_7, 16 bits wide
  assign and_8_out = {16{not_7_out[15]}} & resultado_not;  // AND_Gate and_8, 16 bits wide
  assign and_9_out = {16{not_8_out[15]}} & resultado_left_shift;  // AND_Gate and_9, 16 bits wide
  assign and_10_out = {16{not_9_out[15]}} & resultado_right_shift;  // AND_Gate and_10, 16 bits wide
  assign R = and_2_out | and_3_out | and_4_out | and_5_out | and_6_out | and_7_out | and_8_out | and_9_out | and_10_out;  // OR_Gate or_29, 16 bits wide

  // Other names for the same wires on the sheet: b0 = F[0]; b1 = F[1]; b2 = F[2]; b3 = F[3]
endmodule

// 30
module Registradores (
  input  [4:0] A1,
  input  [15:0] D,
  input  E,
  input  C,
  input  R,
  input  [4:0] A2,
  output [15:0] O1,
  output [15:0] O2
);

  wire and_1_out, and_2_out, and_3_out, and_4_out, and_5_out, and_6_out, and_7_out, and_8_out, and_9_out,
       and_10_out, and_11_out, and_12_out, and_13_out, and_14_out, and_15_out, and_16_out, and_17_out,
       and_18_out, and_19_out, and_20_out, and_21_out, and_22_out, and_23_out, and_24_out, and_25_out,
       and_26_out, and_27_out, and_28_out, and_29_out, and_30_out, and_31_out, and_32_out, decoder_1_out0,
       decoder_1_out1, decoder_1_out2, decoder_1_out3, decoder_1_out4, decoder_1_out5, decoder_1_out6,
       decoder_1_out7, decoder_1_out8, decoder_1_out9, decoder_1_out10, decoder_1_out11, decoder_1_out12,
       decoder_1_out13, decoder_1_out14, decoder_1_out15, decoder_1_out16, decoder_1_out17, decoder_1_out18,
       decoder_1_out19, decoder_1_out20, decoder_1_out21, decoder_1_out22, decoder_1_out23, decoder_1_out24,
       decoder_1_out25, decoder_1_out26, decoder_1_out27, decoder_1_out28, decoder_1_out29, decoder_1_out30,
       decoder_1_out31;
  wire [15:0] _00, _01, _02, _03, _04, _05, _06, _07, _08, _09, _10, _11, _12, _13, _14, _15, _16, _17, _18,
       _19, _20, _21, _23, _24, _25, _26, _27, _28, _29, _30, _31;

  Decoder #(.select(5)) decoder_1 (
    .out0(decoder_1_out0), .out1(decoder_1_out1), .out2(decoder_1_out2), .out3(decoder_1_out3),
    .out4(decoder_1_out4), .out5(decoder_1_out5), .out6(decoder_1_out6), .out7(decoder_1_out7),
    .out8(decoder_1_out8), .out9(decoder_1_out9), .out10(decoder_1_out10), .out11(decoder_1_out11),
    .out12(decoder_1_out12), .out13(decoder_1_out13), .out14(decoder_1_out14), .out15(decoder_1_out15),
    .out16(decoder_1_out16), .out17(decoder_1_out17), .out18(decoder_1_out18), .out19(decoder_1_out19),
    .out20(decoder_1_out20), .out21(decoder_1_out21), .out22(decoder_1_out22), .out23(decoder_1_out23),
    .out24(decoder_1_out24), .out25(decoder_1_out25), .out26(decoder_1_out26), .out27(decoder_1_out27),
    .out28(decoder_1_out28), .out29(decoder_1_out29), .out30(decoder_1_out30), .out31(decoder_1_out31),
    .sel(A1));  // open: en
  and and_1 (and_1_out, decoder_1_out0, E);
  Register #(.width(16)) register_1 (.D(D), .en(and_1_out), .Q(_00), .clk(C), .clr(R));
  Register #(.width(16)) register_2 (.D(D), .en(and_2_out), .Q(_01), .clk(C), .clr(R));
  and and_2 (and_2_out, decoder_1_out1, E);
  and and_3 (and_3_out, decoder_1_out2, E);
  SuperMux supermux_1 (
    .in_1(_31), .in_2(_30), .in_3(_29), .in_4(_28), .in_5(_27), .in_6(_26), .in_7(_25), .in_8(_24),
    .in_10(_23), .in_11(_21), .in_12(_21), .in_13(_20), .in_14(_19), .in_15(_18), .in_16(_17), .in_17(_16),
    .in_18(_15), .in_19(_14), .in_20(_13), .in_21(_12), .in_22(_11), .in_24(_10), .in_25(_09), .in_26(_08),
    .in_27(_07), .in_28(_06), .in_29(_05), .in_30(_04), .in_31(_03), .in_32(_02), .in_33(_01), .in_34(_00),
    .in_9(A1), .in_23(A2), .out_35(O2), .out_36(O1));
  Register #(.width(16)) register_3 (.D(D), .en(and_3_out), .Q(_02), .clk(C), .clr(R));
  Register #(.width(16)) register_4 (.D(D), .en(and_4_out), .Q(_03), .clk(C), .clr(R));
  and and_4 (and_4_out, decoder_1_out3, E);
  and and_5 (and_5_out, decoder_1_out4, E);
  Register #(.width(16)) register_5 (.D(D), .en(and_5_out), .Q(_04), .clk(C), .clr(R));
  Register #(.width(16)) register_6 (.D(D), .en(and_6_out), .Q(_05), .clk(C), .clr(R));
  and and_6 (and_6_out, decoder_1_out5, E);
  and and_7 (and_7_out, decoder_1_out6, E);
  Register #(.width(16)) register_7 (.D(D), .en(and_7_out), .Q(_06), .clk(C), .clr(R));
  Register #(.width(16)) register_8 (.D(D), .en(and_8_out), .Q(_07), .clk(C), .clr(R));
  and and_8 (and_8_out, decoder_1_out7, E);
  and and_9 (and_9_out, decoder_1_out8, E);
  Register #(.width(16)) register_9 (.D(D), .en(and_9_out), .Q(_08), .clk(C), .clr(R));
  Register #(.width(16)) register_10 (.D(D), .en(and_10_out), .Q(_09), .clk(C), .clr(R));
  and and_10 (and_10_out, decoder_1_out9, E);
  and and_11 (and_11_out, decoder_1_out10, E);
  Register #(.width(16)) register_11 (.D(D), .en(and_11_out), .Q(_10), .clk(C), .clr(R));
  Register #(.width(16)) register_12 (.D(D), .en(and_12_out), .Q(_11), .clk(C), .clr(R));
  and and_12 (and_12_out, decoder_1_out11, E);
  and and_13 (and_13_out, decoder_1_out12, E);
  Register #(.width(16)) register_13 (.D(D), .en(and_13_out), .Q(_12), .clk(C), .clr(R));
  Register #(.width(16)) register_14 (.D(D), .en(and_14_out), .Q(_13), .clk(C), .clr(R));
  and and_14 (and_14_out, decoder_1_out13, E);
  Register #(.width(16)) register_15 (.D(D), .en(and_15_out), .Q(_14), .clk(C), .clr(R));
  and and_15 (and_15_out, decoder_1_out14, E);
  and and_16 (and_16_out, decoder_1_out15, E);
  Register #(.width(16)) register_16 (.D(D), .en(and_16_out), .Q(_15), .clk(C), .clr(R));
  Register #(.width(16)) register_17 (.D(D), .en(and_17_out), .Q(_16), .clk(C), .clr(R));
  and and_17 (and_17_out, decoder_1_out16, E);
  and and_18 (and_18_out, decoder_1_out17, E);
  Register #(.width(16)) register_18 (.D(D), .en(and_18_out), .Q(_17), .clk(C), .clr(R));
  Register #(.width(16)) register_19 (.D(D), .en(and_19_out), .Q(_18), .clk(C), .clr(R));
  and and_19 (and_19_out, decoder_1_out18, E);
  and and_20 (and_20_out, decoder_1_out19, E);
  Register #(.width(16)) register_20 (.D(D), .en(and_20_out), .Q(_19), .clk(C), .clr(R));
  Register #(.width(16)) register_21 (.D(D), .en(and_21_out), .Q(_20), .clk(C), .clr(R));
  and and_21 (and_21_out, decoder_1_out20, E);
  and and_22 (and_22_out, decoder_1_out21, E);
  Register #(.width(16)) register_22 (.D(D), .en(and_22_out), .Q(_21), .clk(C), .clr(R));
  Register #(.width(16)) register_23 (.D(D), .en(and_23_out), .Q(_21), .clk(C), .clr(R));
  and and_23 (and_23_out, decoder_1_out22, E);
  and and_24 (and_24_out, decoder_1_out23, E);
  Register #(.width(16)) register_24 (.D(D), .en(and_24_out), .Q(_23), .clk(C), .clr(R));
  Register #(.width(16)) register_25 (.D(D), .en(and_25_out), .Q(_24), .clk(C), .clr(R));
  and and_25 (and_25_out, decoder_1_out24, E);
  and and_26 (and_26_out, decoder_1_out25, E);
  Register #(.width(16)) register_26 (.D(D), .en(and_26_out), .Q(_25), .clk(C), .clr(R));
  Register #(.width(16)) register_27 (.D(D), .en(and_27_out), .Q(_26), .clk(C), .clr(R));
  and and_27 (and_27_out, decoder_1_out26, E);
  and and_28 (and_28_out, decoder_1_out27, E);
  Register #(.width(16)) register_28 (.D(D), .en(and_28_out), .Q(_27), .clk(C), .clr(R));
  Register #(.width(16)) register_29 (.D(D), .en(and_29_out), .Q(_28), .clk(C), .clr(R));
  and and_29 (and_29_out, decoder_1_out28, E);
  and and_30 (and_30_out, decoder_1_out29, E);
  Register #(.width(16)) register_30 (.D(D), .en(and_30_out), .Q(_29), .clk(C), .clr(R));
  and and_31 (and_31_out, decoder_1_out30, E);
  Register #(.width(16)) register_31 (.D(D), .en(and_31_out), .Q(_30), .clk(C), .clr(R));
  Register #(.width(16)) register_32 (.D(D), .en(and_32_out), .Q(_31), .clk(C), .clr(R));
  and and_32 (and_32_out, decoder_1_out31, E);

  // Other names for the same wires on the sheet: _22[15:0] = _21
endmodule

module SuperMux (
  input  [15:0] in_1,
  input  [15:0] in_2,
  input  [15:0] in_3,
  input  [15:0] in_4,
  input  [15:0] in_5,
  input  [15:0] in_6,
  input  [15:0] in_7,
  input  [15:0] in_8,
  input  [4:0] in_9,
  input  [15:0] in_10,
  input  [15:0] in_11,
  input  [15:0] in_12,
  input  [15:0] in_13,
  input  [15:0] in_14,
  input  [15:0] in_15,
  input  [15:0] in_16,
  input  [15:0] in_17,
  input  [15:0] in_18,
  input  [15:0] in_19,
  input  [15:0] in_20,
  input  [15:0] in_21,
  input  [15:0] in_22,
  input  [4:0] in_23,
  input  [15:0] in_24,
  input  [15:0] in_25,
  input  [15:0] in_26,
  input  [15:0] in_27,
  input  [15:0] in_28,
  input  [15:0] in_29,
  input  [15:0] in_30,
  input  [15:0] in_31,
  input  [15:0] in_32,
  input  [15:0] in_33,
  input  [15:0] in_34,
  output [15:0] out_35,
  output [15:0] out_36
);

  Multiplexer #(.select(5), .width(16)) multiplexer_1 (
    .in0(in_34), .in1(in_33), .in2(in_32), .in3(in_31), .in4(in_30), .in5(in_29), .in6(in_28), .in7(in_27),
    .in8(in_26), .in9(in_25), .in10(in_24), .in11(in_22), .in12(in_21), .in13(in_20), .in14(in_19),
    .in15(in_18), .in16(in_17), .in17(in_16), .in18(in_15), .in19(in_14), .in20(in_13), .in21(in_12),
    .in22(in_11), .in23(in_10), .in24(in_8), .in25(in_7), .in26(in_6), .in27(in_5), .in28(in_4), .in29(in_3),
    .in30(in_2), .in31(in_1), .out(out_35), .sel(in_9));  // open: en
  Multiplexer #(.select(5), .width(16)) multiplexer_2 (
    .in0(in_34), .in1(in_33), .in2(in_32), .in3(in_31), .in4(in_30), .in5(in_29), .in6(in_28), .in7(in_27),
    .in8(in_26), .in9(in_25), .in10(in_24), .in11(in_22), .in12(in_21), .in13(in_20), .in14(in_19),
    .in15(in_18), .in16(in_17), .in17(in_16), .in18(in_15), .in19(in_14), .in20(in_13), .in21(in_12),
    .in22(in_11), .in23(in_10), .in24(in_8), .in25(in_7), .in26(in_6), .in27(in_5), .in28(in_4), .in29(in_3),
    .in30(in_2), .in31(in_1), .out(out_36), .sel(in_23));  // open: en

  // Other names for the same wires on the sheet: _00[15:0] = in_34; _01[15:0] = in_33; _02[15:0] = in_32;
  //   _03[15:0] = in_31; _04[15:0] = in_30; _05[15:0] = in_29; _06[15:0] = in_28; _07[15:0] = in_27;
  //   _08[15:0] = in_26; _09[15:0] = in_25; _10[15:0] = in_24; _11[15:0] = in_22; _12[15:0] = in_21;
  //   _13[15:0] = in_20; _14[15:0] = in_19; _15[15:0] = in_18; _16[15:0] = in_17; _17[15:0] = in_16;
  //   _18[15:0] = in_15; _19[15:0] = in_14; _20[15:0] = in_13; _21[15:0] = in_12; _22[15:0] = in_11;
  //   _23[15:0] = in_10; _24[15:0] = in_8; _25[15:0] = in_7; _26[15:0] = in_6; _27[15:0] = in_5; _28[15:0] = in_4;
  //   _29[15:0] = in_3; _30[15:0] = in_2; _31[15:0] = in_1
endmodule

module Processor (
  input  reset,
  input  clock,
  input  [15:0] ins,
  output [11:0] out_4
);

  wire add, \and , and_13_out, and_14_out, and_15_out, cmp, cmp_flag_e, cmp_flag_g, div, En, Fle, Flg, je,
       jg, jmp, jne, mov, movcons, mul, \not , not_1_out, not_2_out, not_3_out, not_4_out, not_5_out,
       not_6_out, not_7_out, not_8_out, not_9_out, not_10_out, not_11_out, not_12_out, not_13_out,
       not_14_out, not_15_out, not_16_out, not_17_out, not_18_out, not_19_out, not_20_out, not_21_out,
       not_22_out, not_23_out, not_24_out, not_25_out, not_26_out, not_27_out, not_28_out, not_29_out,
       not_30_out, not_31_out, not_32_out, not_33_out, not_34_out, not_35_out, not_36_out, not_37_out,
       not_38_out, not_40_out, \or , or_3_out, pc_count, pc_load, shl, shr, sub;
  wire [1:0] not_41_out;
  wire [4:0] Add1;
  wire [15:0] A, B, bit_extender_1_out, Data, Res;

  not not_1 (not_1_out, ins[10]);
  not not_2 (not_2_out, ins[14]);
  not not_3 (not_3_out, ins[13]);
  not not_4 (not_4_out, ins[14]);
  not not_5 (not_5_out, ins[10]);
  not not_6 (not_6_out, ins[11]);
  not not_7 (not_7_out, ins[12]);
  not not_8 (not_8_out, ins[14]);
  not not_9 (not_9_out, ins[15]);
  not not_10 (not_10_out, ins[11]);
  not not_11 (not_11_out, ins[12]);
  not not_12 (not_12_out, ins[14]);
  not not_13 (not_13_out, ins[15]);
  not not_14 (not_14_out, ins[10]);
  not not_15 (not_15_out, ins[12]);
  not not_16 (not_16_out, ins[14]);
  not not_17 (not_17_out, ins[15]);
  not not_18 (not_18_out, ins[12]);
  not not_19 (not_19_out, ins[14]);
  not not_20 (not_20_out, ins[15]);
  not not_21 (not_21_out, ins[10]);
  not not_22 (not_22_out, ins[11]);
  not not_23 (not_23_out, ins[14]);
  not not_24 (not_24_out, ins[15]);
  not not_25 (not_25_out, ins[11]);
  not not_26 (not_26_out, ins[14]);
  not not_27 (not_27_out, ins[15]);
  not not_28 (not_28_out, ins[10]);
  not not_29 (not_29_out, ins[14]);
  not not_30 (not_30_out, ins[15]);
  and and_1 (\or , ins[10], ins[11], ins[12], not_31_out, not_32_out, ins[13]);
  not not_31 (not_31_out, ins[14]);
  not not_32 (not_32_out, ins[15]);
  not not_33 (not_33_out, ins[10]);
  not not_34 (not_34_out, ins[12]);
  and and_2 (\not , not_33_out, ins[11], not_34_out, not_35_out, ins[15], ins[13]);
  not not_35 (not_35_out, ins[14]);
  not not_36 (not_36_out, ins[11]);
  not not_37 (not_37_out, ins[12]);
  and and_3 (mov, not_1_out, not_36_out, not_37_out, not_2_out, ins[15], ins[13]);
  and and_4 (movcons, not_3_out, not_4_out, ins[15]);
  and and_5 (add, not_5_out, not_6_out, not_7_out, not_8_out, not_9_out, ins[13]);
  and and_6 (sub, ins[10], not_10_out, not_11_out, not_12_out, not_13_out, ins[13]);
  and and_7 (mul, not_14_out, ins[11], not_15_out, not_16_out, not_17_out, ins[13]);
  and and_8 (div, ins[10], ins[11], not_18_out, not_19_out, not_20_out, ins[13]);
  and and_9 (shl, not_21_out, not_22_out, ins[12], not_23_out, not_24_out, ins[13]);
  and and_10 (shr, ins[10], not_25_out, ins[12], not_26_out, not_27_out, ins[13]);
  and and_11 (\and , not_28_out, ins[11], ins[12], not_29_out, not_30_out, ins[13]);
  Counter #(.width(12), .max('hfff)) counter_1 (
    .load(pc_load), .D(ins[11:0]), .count(pc_count), .Q(out_4), .clk(clock), .clr(reset));  // open: carry
  and and_12 (je, ~ins[12], ~ins[13], ins[14], ins[15]);  // AND_Gate
  Register #(.width(1)) register_1 (.D(Flg), .en(cmp), .Q(cmp_flag_g), .clk(clock), .clr(reset));
  Register #(.width(1)) register_2 (.D(Fle), .en(cmp), .Q(cmp_flag_e), .clk(clock), .clr(reset));
  and and_13 (and_13_out, je, cmp_flag_e);
  and and_14 (and_14_out, jne, not_38_out);
  not not_38 (not_38_out, cmp_flag_e);
  and and_15 (and_15_out, jg, cmp_flag_g);
  and and_16 (cmp, ins[10], ~ins[11], ~ins[12], ins[13], ~ins[14], ins[15]);  // AND_Gate
  // Probe on ins[11:0]
  Registradores registradores_1 (.D(Data), .E(En), .C(clock), .R(reset), .A2(ins[4:0]), .O1(B), .O2(A), .A1(Add1));
  or or_1 (pc_load, jmp, and_13_out, and_14_out, and_15_out);
  and and_17 (jmp, ins[12], ins[13], ins[14], ins[15]);
  and and_18 (jg, ~ins[12], ins[13], ins[14], ins[15]);  // AND_Gate
  and and_19 (jne, ins[12], ~ins[13], ins[14], ins[15]);  // AND_Gate
  ULA ula_1 (.A(A), .F(ins[13:10]), .B(B), .R(Res), .FG(Flg), .FE(Fle));
  Multiplexer #(.width(5)) multiplexer_1 (.in0(ins[9:5]), .in1(ins[4:0]), .out(Add1), .sel(movcons));  // open: en
  not not_39 (pc_count, pc_load);
  // Probe on Data
  // Probe on Add1
  // Probe on ins[4:0]
  // Probe on A
  // Probe on B
  // Probe on ins[13:10]
  // Probe on Res
  or or_2 (En, movcons, sub, add, mul, div, shl, shr, \and , \or , \not , mov);
  assign bit_extender_1_out = {{8{1'b0}}, ins[12:5]};  // Bit_Extender bit_extender_1
  or or_3 (or_3_out, movcons, mov);
  not not_40 (not_40_out, movcons);
  and and_20 (not_41_out[1], not_40_out, mov);
  not not_41 (not_41_out[0], or_3_out);
  // Probe on Data
  Multiplexer #(.select(2), .width(16)) multiplexer_2 (
    .in0(bit_extender_1_out), .in1(Res), .in2(B), .out(Data), .sel(not_41_out));  // open: in3, en
  RAM #(.dataWidth(16)) ram_1 ();  // open: addr, data, sel, clk, ld, clr

  // Other names for the same wires on the sheet: clk = clock; con[7:0] = ins[12:5]; Op[3:0] = ins[13:10];
  //   pc[11:0] = out_4; Add2[4:0] = ins[4:0]; label[11:0] = ins[11:0]; pc_data[11:0] = ins[11:0];
  //   reg2[4:0] = ins[4:0]; reg1[4:0] = ins[9:5]; Q1[15:0] = A; Q2[15:0] = B; Rs = reset

  // Notes on the sheet:
  //   RISC Lukitias
endmodule
